// Logisim project aquecedor.circ as structural Verilog: 4 circuits, main circuit main
module main (
  input  BO,
  input  BL
);

  wire BM_out;

  Button BM (.out(BM_out));
  aquecedor aquecedor_1 (.BO(BO), .BL(BL), .BM(BM_out));  // open: SD, SE, R2, R1, MV
endmodule

module modo_funcionamento (
  input  CLK,
  input  BL,
  input  BM,
  output R2,
  output R1,
  output MV
);

  wire and_1_out, and_2_out, and_3_out, and_4_out, and_5_out, and_6_out, JK0_q, JK0_qn, JK1_q, JK1_qn,
       not_1_out, not_2_out, or_1_out, or_2_out, or_3_out;

  and and_1 (and_1_out, BL, BM, JK0_q);
  and and_2 (and_2_out, BM, JK0_q);
  and and_3 (and_3_out, BM, BL);
  and and_4 (and_4_out, BL, JK1_qn);
  and and_5 (and_5_out, BM, JK1_qn);
  not not_1 (not_1_out, BL);
  or or_1 (or_1_out, and_2_out, not_2_out);
  not not_2 (not_2_out, BL);
  or or_2 (or_2_out, and_3_out, and_4_out);
  or or_3 (or_3_out, and_5_out, not_1_out);
  J_K_Flip_Flop JK1 (.J(and_1_out), .K(or_1_out), .clk(CLK), .Q(JK1_q), .Qn(JK1_qn));  // open: preset, reset
  J_K_Flip_Flop JK0 (.J(or_2_out), .K(or_3_out), .clk(CLK), .Q(JK0_q), .Qn(JK0_qn));  // open: preset, reset
  and and_6 (and_6_out, JK0_q, JK1_qn);
  and and_7 (R2, JK1_q, JK0_qn);
  or or_4 (R1, and_6_out, R2);
  or or_5 (MV, JK1_q, JK0_q);
endmodule

module motor_oscilacao (
  input  CLK,
  input  MO,
  output SD,
  output SE
);

  wire and_1_out, and_2_out, and_3_out, and_4_out, and_5_out, and_6_out, and_7_out, and_8_out, and_9_out,
       not_1_out, or_1_out, or_2_out, or_3_out, T0_q, T0_qn, T1_q, T1_qn, T2_q, T2_qn;

  and and_1 (and_1_out, T2_q, T0_qn, T1_qn);
  and and_2 (and_2_out, MO, T2_qn, T1_q, T0_q);
  and and_3 (and_3_out, T2_q, T1_q);
  or or_1 (or_1_out, and_1_out, and_2_out);
  and and_4 (and_4_out, MO, T2_qn, T0_q);
  not not_1 (not_1_out, MO);
  or or_2 (or_2_out, T0_q, and_3_out, MO);
  and and_5 (and_5_out, not_1_out, T2_qn, T1_q);
  or or_3 (or_3_out, and_4_out, and_5_out);
  T_Flip_Flop T2 (.T(or_1_out), .clk(CLK), .Q(T2_q), .Qn(T2_qn));  // open: reset, preset
  T_Flip_Flop T1 (.T(or_3_out), .clk(CLK), .Q(T1_q), .Qn(T1_qn));  // open: reset, preset
  T_Flip_Flop T0 (.T(or_2_out), .clk(CLK), .Q(T0_q), .Qn(T0_qn));  // open: reset, preset
  and and_6 (and_6_out, T2_qn, T1_qn, T0_q);
  and and_7 (and_7_out, T2_qn, T1_q, T0_qn);
  and and_8 (and_8_out, T2_qn, T1_q, T0_q);
  and and_9 (and_9_out, T2_q, T1_qn, T0_qn);
  or or_4 (SD, and_6_out, and_7_out);
  or or_5 (SE, and_8_out, and_9_out);
endmodule

module aquecedor (
  input  BO,
  input  BL,
  input  BM,
  output SD,
  output SE,
  output R2,
  output R1,
  output MV
);

  wire and_1_out, clock_1_out;

  Clock clock_1 (.out(clock_1_out));
  and and_1 (and_1_out, BO, BL);
  motor_oscilacao motor_oscilacao_1 (.CLK(clock_1_out), .MO(and_1_out), .SD(SD), .SE(SE));
  modo_funcionamento modo_funcionamento_1 (.CLK(clock_1_out), .BL(BL), .BM(BM), .R2(R2), .R1(R1), .MV(MV));
endmodule
